# Fritzing sketch Sembrani (saved by Fritzing 0.9.3b)
breadboards: 1

parts:
  M1 = DOIT Esp32 DevKit v1 (30 pins long, 11 pins width) [part_number=ESP32S-PIN30]
  J1 = Piezo Speaker
  U1 = Sharp PC817 [package=THT]
  R1 = Resistor [tolerance=±5% resistance=220 package=THT]
  BAT1 = 12 battery [package=battery]
  SC2272 = SC2272 [chip_label=SC2272 package="SIP (Single Inline) [THT]"]
  U2 = Mini-360 DC-DC Buck converter [package=THT]

nets:
  N1: M1.D25, SC2272.D3
  N2: M1.D26, SC2272.D2
  N3: M1.D27, SC2272.D1
  N4: M1.D14, SC2272.D0
  N5: M1.D12, SC2272.VT
  N6: M1.D13, R1.Pin_1
  GND: M1.GND, U1.Pin_1, SC2272.GND, U2.OUT-
  VIN: M1.VIN, SC2272.5v, U2.OUT+
  N7: J1.pin1, BAT1.-, U2.IN-
  N8: J1.pin2, U1.Pin_4
  N9: U1.Pin_2, R1.Pin_0
  N10: U1.Pin_3, BAT1.+, U2.IN+

custom parts:
  DOIT Esp32 DevKit v1 (30 pins long, 11 pins width): The DOIT Esp32 DevKit v1 is one of the development board created by DOIT to evaluate the ESP-WROOM-32 module. It is based on the ESP32 microcontroller that boasts Wifi, Bluetooth, Ethernet and Low Power support all in a single chip. (vanepp) made breadboard work, adjusted pin numbering and labels and reduced size of schematic and cleaned up pcb. This chip is 30pins long (2 x15) and 11 pins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
  12 battery: 12V lead acid type battery, like the Husqvarna YTH2448 12V 35AH battery. This is the mini version 1/4 the size of the actual battery to be closer to typical breadboard parts (around 2in wide rathher than 7in). The pads in pcb are sized to accomidate up to 14ga wire (as these batterys will deliver high currents.)
  SC2272: Simple Part SC2272
  Mini-360 DC-DC Buck converter: Mini-360 DC-DC Buck converter. Tiny buck step down voltage converter, input voltage 4.75 to 23V output 1 to 17V adjustable. Available from ebay and the like.
